# Fritzing sketch shema spoja (saved by Fritzing 1.0.1rc)
breadboards: 3

parts:
  M1 = DOIT Esp32 DevKit v1 (30 pins long, 11 pins width) [part_number=ESP32S-PIN30]
  DHT1 = Humidity and Temperature Sensor DHT11
  R1 = PHOTOCELL [package=photocell]
  Mod1 = Passive Buzzer
  S1 = Momentary Switch [package=ksa_sealed_tac_switch]
  R2 = Resistor [tolerance=±5% resistance=220 package="0603 [SMD]"]
  R3 = Resistor [tolerance=±5% resistance=220 package="0603 [SMD]"]
  R4 = Resistor [tolerance=±5% resistance=10k package="0603 [SMD]"]
  R5 = Resistor [tolerance=±5% resistance=220 package="0603 [SMD]"]
  S2 = H-Bridge with L298N
  LED1 = LEDs [package=led10mm]
  LED2 = LEDs [package=led10mm]
  LED3 = LEDs [package=led10mm]
  J1 = Basic Servo
  F1 = Fan - Ventilador [package=THT]
  VCC1 = Battery block 9V

nets:
  3V3: M1.3V3, DHT1.Vcc, R1.P$1, Mod1.NC
  GND: M1.GND, DHT1.GND, Mod1.-, S1.3, R4.Pin_0, LED1.C, LED2.C, LED3.C, J1.gnd
  N1: M1.D18, J1.pulse
  N2: M1.D19, Mod1.S
  N3: M1.D21, DHT1.Data-signal
  N4: M1.D22, S2.IN2
  N5: M1.D23, S2.ENA, S2.IN1
  N6: M1.D34, R1.P$2, R4.Pin_1
  N7: M1.D33, S1.2
  N8: M1.D25, R2.Pin_0
  N9: M1.D26, R5.Pin_0
  N10: M1.D27, R3.Pin_0
  VIN: M1.VIN, J1.vcc
  N11: R2.Pin_1, LED3.A
  N12: R3.Pin_1, LED2.A
  N13: R5.Pin_1, LED1.A
  N14: S2.12V, VCC1.+
  N15: S2.GND, VCC1.-
  N16: S2.M1-01, F1.GND
  N17: S2.M1-02, F1.5V

custom parts:
  DOIT Esp32 DevKit v1 (30 pins long, 11 pins width): The DOIT Esp32 DevKit v1 is one of the development board created by DOIT to evaluate the ESP-WROOM-32 module. It is based on the ESP32 microcontroller that boasts Wifi, Bluetooth, Ethernet and Low Power support all in a single chip. (vanepp) made breadboard work, adjusted pin numbering and labels and reduced size of schematic and cleaned up pcb. This chip is 30pins long (2 x15) and 11 pins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
  Humidity and Temperature Sensor DHT11: Digital relative humidity & temperature sensor DHT11
  H-Bridge with L298N: h-bridge
  Fan - Ventilador: Ventilador de 2 pines, se encuentra comunmente en computadoras de escritorio
